// Logisim project 12_shift_register.circ as structural Verilog: 1 circuit, main circuit main
module main (
  input  DS,
  input  OE,
  output out_3,
  output out_4,
  output out_5,
  output out_6
);

  wire clock_1_out, d_ff_1_q, d_ff_2_q, d_ff_3_q, d_ff_4_q;

  Clock clock_1 (.out(clock_1_out));
  D_Flip_Flop d_ff_1 (.clk(clock_1_out), .D(DS), .Q(d_ff_1_q));  // open: Qn, preset, en, reset
  and and_1 (out_3, OE, d_ff_1_q);
  D_Flip_Flop d_ff_2 (.clk(clock_1_out), .D(d_ff_1_q), .Q(d_ff_2_q));  // open: Qn, preset, en, reset
  and and_2 (out_4, OE, d_ff_2_q);
  D_Flip_Flop d_ff_3 (.clk(clock_1_out), .D(d_ff_2_q), .Q(d_ff_3_q));  // open: Qn, preset, en, reset
  and and_3 (out_5, OE, d_ff_3_q);
  D_Flip_Flop d_ff_4 (.clk(clock_1_out), .D(d_ff_3_q), .Q(d_ff_4_q));  // open: Qn, preset, en, reset
  and and_4 (out_6, OE, d_ff_4_q);
endmodule
