// Logisim project 14_register_file.circ as structural Verilog: 1 circuit, main circuit main
module main (
  input  [1:0] Read_R1,
  input  [1:0] Write_R1,
  input  [7:0] Data_Input,
  input  [1:0] Read_R2,
  output [7:0] Output_1,
  output [7:0] Output_2
);

  wire clock_1_out, decoder_1_out0, decoder_1_out1, decoder_1_out2, decoder_1_out3;
  wire [7:0] demultiplexer_1_out0, demultiplexer_1_out1, demultiplexer_1_out2, demultiplexer_1_out3,
       register_1_q, register_2_q, register_3_q, register_4_q;

  Demultiplexer #(.select(2), .width(8), .enable("false")) demultiplexer_1 (
    .out0(demultiplexer_1_out0), .out1(demultiplexer_1_out1), .out2(demultiplexer_1_out2),
    .out3(demultiplexer_1_out3), .in(Data_Input), .sel(Write_R1));
  Decoder #(.select(2), .enable("false")) decoder_1 (
    .out0(decoder_1_out0), .out1(decoder_1_out1), .out2(decoder_1_out2), .out3(decoder_1_out3), .sel(Write_R1));
  Clock clock_1 (.out(clock_1_out));
  Register register_1 (
    .D(demultiplexer_1_out0), .en(decoder_1_out0), .Q(register_1_q), .clk(clock_1_out));  // open: clr
  Register register_2 (
    .D(demultiplexer_1_out2), .en(decoder_1_out2), .Q(register_2_q), .clk(clock_1_out));  // open: clr
  Register register_3 (
    .D(demultiplexer_1_out1), .en(decoder_1_out1), .Q(register_3_q), .clk(clock_1_out));  // open: clr
  Register register_4 (
    .D(demultiplexer_1_out3), .en(decoder_1_out3), .Q(register_4_q), .clk(clock_1_out));  // open: clr
  Multiplexer #(.select(2), .width(8), .enable("false")) multiplexer_1 (
    .in0(register_1_q), .in1(register_3_q), .in2(register_2_q), .in3(register_4_q), .out(Output_1),
    .sel(Read_R1));
  Multiplexer #(.select(2), .width(8), .enable("false")) multiplexer_2 (
    .in0(register_1_q), .in1(register_3_q), .in2(register_2_q), .in3(register_4_q), .out(Output_2),
    .sel(Read_R2));

  // Notes on the sheet:
  //   Archivo de registros (4 x 8 bits)
endmodule
