// Logisim project 15_deco_dmx.circ as structural Verilog: 1 circuit, main circuit main
module main (
  input  in_1,
  input  in_2,
  input  in_3,
  input  in_4,
  input  DATA,
  output out_6,
  output out_7,
  output out_8,
  output out_9,
  output out_10,
  output out_11,
  output out_12,
  output out_13
);

  and and_1 (out_6, ~in_1, ~in_2);  // AND_Gate
  and and_2 (out_8, ~in_1, in_2);  // AND_Gate
  and and_3 (out_10, in_1, ~in_2);  // AND_Gate
  and and_4 (out_12, in_1, in_2);
  Decoder #(.select(2), .enable("false")) decoder_1 ();  // open: out0, out1, out2, out3, sel
  Demultiplexer #(.select(2), .enable("false")) demultiplexer_1 ();  // open: out0, out1, out2, out3, in, sel
  and and_5 (out_7, ~in_3, DATA, ~in_4);  // AND_Gate
  and and_6 (out_9, ~in_3, DATA, in_4);  // AND_Gate
  and and_7 (out_11, in_3, DATA, ~in_4);  // AND_Gate
  and and_8 (out_13, in_3, DATA, in_4);

  // Notes on the sheet:
  //   Decodificador 2:4
  //   Demultiplexor 1:4
endmodule
